// Logisim project CPU1_v2.circ as structural Verilog: 1 circuit, main circuit main
module main (
  input  Bus_Override,
  input  in_2,
  input  in_3,
  input  in_4
);

  wire A_In, B_In, Clock, n7_segment_display_1_p1, n7_segment_display_2_p1, n7_segment_display_3_p1,
       n7_segment_display_4_p1, n7_segment_display_5_p1, n7_segment_display_6_p1, n7_segment_display_7_p1,
       n7_segment_display_8_p1, n7_segment_display_9_p1, Reset;
  wire [7:0] binary_to_bcd_converter_1_p1, counter_1_q, dipswitch_1_sw1;

  Button button_1 (.out(Reset));
  Button button_2 (.out(Clock));
  LED b1 (.in(binary_to_bcd_converter_1_p1[0]));
  LED b2 (.in(binary_to_bcd_converter_1_p1[1]));
  LED b4 (.in(binary_to_bcd_converter_1_p1[2]));
  LED b8 (.in(binary_to_bcd_converter_1_p1[3]));
  LED b16 (.in(binary_to_bcd_converter_1_p1[4]));
  LED b128 (.in(binary_to_bcd_converter_1_p1[7]));
  LED b32 (.in(binary_to_bcd_converter_1_p1[5]));
  LED b64 (.in(binary_to_bcd_converter_1_p1[6]));
  // _7_Segment_Display 7_segment_display_1: pin names not known; wires that end beside it: n7_segment_display_1_p1, n7_segment_display_1_p1
  // BCD_to_7_Segment_decoder bcd_to_7_segment_decoder_1: pin names not known
  // Binary_to_BCD_converter #(.binvalue(8)) binary_to_bcd_converter_1: pin names not known; wires that end beside it: binary_to_bcd_converter_1_p1
  Pull_Resistor pull_resistor_1 (.node(binary_to_bcd_converter_1_p1));
  // _7_Segment_Display 7_segment_display_2: pin names not known; wires that end beside it: n7_segment_display_2_p1, n7_segment_display_2_p1
  // BCD_to_7_Segment_decoder bcd_to_7_segment_decoder_2: pin names not known
  // _7_Segment_Display 7_segment_display_3: pin names not known; wires that end beside it: n7_segment_display_3_p1, n7_segment_display_3_p1
  // BCD_to_7_Segment_decoder bcd_to_7_segment_decoder_3: pin names not known
  assign binary_to_bcd_converter_1_p1 = Bus_Override ? dipswitch_1_sw1 : 8'bz;  // Controlled_Buffer controlled_buffer_1
  DipSwitch dipswitch_1 (
    .sw1(dipswitch_1_sw1[0]), .sw2(dipswitch_1_sw1[1]), .sw3(dipswitch_1_sw1[2]), .sw4(dipswitch_1_sw1[3]),
    .sw5(dipswitch_1_sw1[4]), .sw6(dipswitch_1_sw1[5]), .sw7(dipswitch_1_sw1[6]), .sw8(dipswitch_1_sw1[7]));
  Counter counter_1 (
    .clr(Reset), .load(in_2), .up(1'b1), .count(in_4), .clk(Clock), .D(binary_to_bcd_converter_1_p1),
    .Q(counter_1_q));  // open: carry
  Register Register_A (.en(A_In), .clk(Clock), .clr(Reset));  // open: D, Q
  Register Register_B (.en(B_In), .clk(Clock), .clr(Reset));  // open: D, Q
  LED led_1 ();  // open: in
  LED led_2 ();  // open: in
  LED led_3 ();  // open: in
  LED led_4 ();  // open: in
  LED led_5 ();  // open: in
  // _7_Segment_Display 7_segment_display_4: pin names not known; wires that end beside it: n7_segment_display_4_p1, n7_segment_display_4_p1
  // BCD_to_7_Segment_decoder bcd_to_7_segment_decoder_4: pin names not known
  // Binary_to_BCD_converter #(.binvalue(8)) binary_to_bcd_converter_2: pin names not known; wires that end beside it: counter_1_q
  assign binary_to_bcd_converter_1_p1 = in_3 ? counter_1_q : 8'bz;  // Controlled_Buffer controlled_buffer_2
  LED led_6 ();  // open: in
  LED led_7 ();  // open: in
  LED led_8 ();  // open: in
  // _7_Segment_Display 7_segment_display_5: pin names not known; wires that end beside it: n7_segment_display_5_p1, n7_segment_display_5_p1
  // BCD_to_7_Segment_decoder bcd_to_7_segment_decoder_5: pin names not known
  // _7_Segment_Display 7_segment_display_6: pin names not known; wires that end beside it: n7_segment_display_6_p1, n7_segment_display_6_p1
  // BCD_to_7_Segment_decoder bcd_to_7_segment_decoder_6: pin names not known
  // _7_Segment_Display 7_segment_display_7: pin names not known; wires that end beside it: n7_segment_display_7_p1, n7_segment_display_7_p1
  // BCD_to_7_Segment_decoder bcd_to_7_segment_decoder_7: pin names not known
  // Binary_to_BCD_converter #(.binvalue(8)) binary_to_bcd_converter_3: pin names not known
  // _7_Segment_Display 7_segment_display_8: pin names not known; wires that end beside it: n7_segment_display_8_p1, n7_segment_display_8_p1
  // _7_Segment_Display 7_segment_display_9: pin names not known; wires that end beside it: n7_segment_display_9_p1, n7_segment_display_9_p1
  // BCD_to_7_Segment_decoder bcd_to_7_segment_decoder_8: pin names not known
  // BCD_to_7_Segment_decoder bcd_to_7_segment_decoder_9: pin names not known

  // Other names for the same wires on the sheet: Counter_Enable = in_4; Counter_In = in_2; Counter_Out = in_3
endmodule
