// Logisim project CPU1_v4.circ as structural Verilog: 1 circuit, main circuit main
module main (
  input  in_1,
  input  in_2,
  input  in_3,
  input  in_4,
  input  in_5,
  input  in_6,
  input  in_7,
  input  in_8,
  input  [3:0] in_9,
  output [7:0] out_10,
  output [7:0] out_11,
  output [7:0] out_12,
  output [7:0] out_13,
  output [7:0] out_14,
  output [7:0] out_15
);

  wire bcd_to_7_segment_decoder_7_p2, bcd_to_7_segment_decoder_7_p3, bcd_to_7_segment_decoder_7_p4,
       binary_to_bcd_converter_3_p1, Clock, decoder_1_out0, decoder_1_out1, decoder_1_out2, decoder_1_out3,
       decoder_1_out4, decoder_1_out5, decoder_1_out6, decoder_1_out7, decoder_1_out8, decoder_1_out9,
       decoder_1_out10, decoder_1_out11, decoder_1_out12, decoder_1_out13, n7_segment_display_1_p1,
       n7_segment_display_2_p1, n7_segment_display_3_p1, n7_segment_display_4_p1, n7_segment_display_5_p1,
       n7_segment_display_6_p1, n7_segment_display_7_p1, n7_segment_display_8_p1, n7_segment_display_9_p1,
       Reset, undriven_4, undriven_5;
  wire [7:0] and_1_out, Bus_Override, controlled_buffer_3_out, controlled_buffer_4_out,
       controlled_buffer_5_out, controlled_buffer_6_out, counter_1_q, d_ff_1_q, dipswitch_1_sw1, not_1_out,
       not_2_out, not_3_out, not_4_out, not_5_out, or_1_out, register_1_q, register_2_q, register_3_q,
       undriven, undriven_2, undriven_3, xor_1_out;

  Button button_1 (.out(Reset));
  Button button_2 (.out(Clock));
  DipSwitch dipswitch_1 (
    .sw1(dipswitch_1_sw1[0]), .sw2(dipswitch_1_sw1[1]), .sw3(dipswitch_1_sw1[2]), .sw4(dipswitch_1_sw1[3]),
    .sw5(dipswitch_1_sw1[4]), .sw6(dipswitch_1_sw1[5]), .sw7(dipswitch_1_sw1[6]), .sw8(dipswitch_1_sw1[7]));
  assign Bus_Override = in_1 ? dipswitch_1_sw1 : 8'bz;  // Controlled_Buffer controlled_buffer_1
  ROM #(.dataWidth(16)) Microcode ();  // open: addr, data
  LED led_1 (.in(Bus_Override[7]));
  LED led_2 (.in(Bus_Override[6]));
  LED led_3 (.in(Bus_Override[5]));
  LED led_4 (.in(Bus_Override[4]));
  LED led_5 (.in(Bus_Override[3]));
  LED led_6 (.in(Bus_Override[2]));
  LED led_7 (.in(Bus_Override[0]));
  LED led_8 (.in(Bus_Override[1]));
  Pull_Resistor pull_resistor_1 (.node(Bus_Override));
  // _7_Segment_Display 7_segment_display_1: pin names not known; wires that end beside it: n7_segment_display_1_p1, n7_segment_display_1_p1
  // _7_Segment_Display 7_segment_display_2: pin names not known; wires that end beside it: n7_segment_display_2_p1, n7_segment_display_2_p1
  // BCD_to_7_Segment_decoder bcd_to_7_segment_decoder_1: pin names not known
  // BCD_to_7_Segment_decoder bcd_to_7_segment_decoder_2: pin names not known
  // Binary_to_BCD_converter #(.binvalue(8)) binary_to_bcd_converter_1: pin names not known; wires that end beside it: Bus_Override
  // _7_Segment_Display 7_segment_display_3: pin names not known; wires that end beside it: n7_segment_display_3_p1, n7_segment_display_3_p1
  // BCD_to_7_Segment_decoder bcd_to_7_segment_decoder_3: pin names not known
  Counter counter_1 (
    .clr(Reset), .load(in_2), .up(1'b1), .count(in_4), .clk(Clock), .D(Bus_Override), .Q(counter_1_q));  // open: carry
  assign Bus_Override = in_3 ? counter_1_q : 8'bz;  // Controlled_Buffer controlled_buffer_2
  Adder adder_1 (.a(register_1_q), .b(register_2_q), .out(out_10));  // open: cin, cout
  // _7_Segment_Display 7_segment_display_4: pin names not known; wires that end beside it: n7_segment_display_4_p1, n7_segment_display_4_p1
  // BCD_to_7_Segment_decoder bcd_to_7_segment_decoder_4: pin names not known
  // Binary_to_BCD_converter #(.binvalue(8)) binary_to_bcd_converter_2: pin names not known; wires that end beside it: counter_1_q
  LED led_9 (.in(counter_1_q[7]));
  LED led_10 (.in(counter_1_q[6]));
  LED led_11 (.in(register_1_q[7]));
  LED led_12 (.in(register_1_q[6]));
  DotMatrix #(.matrixcols(13), .matrixrows(1)) dotmatrix_1 (
    .col0(decoder_1_out1), .col1(decoder_1_out2), .col2(decoder_1_out3), .col3(decoder_1_out4),
    .col4(decoder_1_out5), .col5(decoder_1_out6), .col6(decoder_1_out7), .col7(decoder_1_out8),
    .col8(decoder_1_out9), .col9(decoder_1_out10), .col10(decoder_1_out11), .col11(decoder_1_out12),
    .col12(decoder_1_out13));
  // _7_Segment_Display 7_segment_display_5: pin names not known; wires that end beside it: n7_segment_display_5_p1, n7_segment_display_5_p1
  // BCD_to_7_Segment_decoder bcd_to_7_segment_decoder_5: pin names not known
  LED led_13 (.in(counter_1_q[5]));
  LED led_14 (.in(counter_1_q[4]));
  LED led_15 (.in(counter_1_q[3]));
  LED led_16 (.in(register_1_q[5]));
  LED led_17 (.in(register_1_q[4]));
  LED led_18 (.in(register_1_q[3]));
  LED led_19 (.in(register_1_q[2]));
  Register register_1 (.D(controlled_buffer_3_out), .en(in_5), .clk(Clock), .Q(register_1_q), .clr(Reset));
  Subtractor subtractor_1 (.a(register_1_q), .b(register_2_q), .out(out_11));  // open: bin, bout
  // _7_Segment_Display 7_segment_display_6: pin names not known; wires that end beside it: n7_segment_display_6_p1, n7_segment_display_6_p1
  // BCD_to_7_Segment_decoder bcd_to_7_segment_decoder_6: pin names not known
  LED led_20 (.in(counter_1_q[2]));
  LED led_21 (.in(counter_1_q[1]));
  LED led_22 (.in(counter_1_q[0]));
  LED led_23 (.in(register_1_q[1]));
  LED led_24 (.in(register_1_q[0]));
  assign controlled_buffer_3_out = in_7 ? register_1_q : 8'bz;  // Controlled_Buffer controlled_buffer_3
  Multiplier multiplier_1 (.a(register_1_q), .b(register_2_q), .out(out_12));  // open: cin, cout
  Decoder #(.select(4)) decoder_1 (
    .out0(decoder_1_out0), .out1(decoder_1_out1), .out2(decoder_1_out2), .out3(decoder_1_out3),
    .out4(decoder_1_out4), .out5(decoder_1_out5), .out6(decoder_1_out6), .out7(decoder_1_out7),
    .out8(decoder_1_out8), .out9(decoder_1_out9), .out10(decoder_1_out10), .out11(decoder_1_out11),
    .out12(decoder_1_out12), .out13(decoder_1_out13), .sel(in_9));  // open: out14, out15, en
  LED led_25 (.in(register_2_q[7]));
  Divider divider_1 (.a(register_1_q), .b(register_2_q), .out(out_13), .rem(out_14));  // open: upper
  LED led_26 (.in(register_2_q[6]));
  LED led_27 (.in(register_2_q[5]));
  LED led_28 (.in(register_2_q[4]));
  LED led_29 (.in(register_2_q[3]));
  Register register_2 (.D(controlled_buffer_4_out), .en(in_6), .clk(Clock), .Q(register_2_q), .clr(Reset));
  Multiplexer #(.enable("false"), .select(4), .width(8)) multiplexer_1 (
    .in1(out_10), .in2(out_11), .in3(out_12), .in4(out_13), .in5(out_14), .in6(and_1_out), .in7(not_1_out),
    .in8(or_1_out), .in9(not_2_out), .in10(xor_1_out), .in11(not_3_out), .in12(not_4_out), .in13(not_5_out),
    .out(out_15), .sel(in_9));  // open: in0, in14, in15
  DotMatrix #(.dotshape("circle"), .matrixcols(1), .matrixrows(8)) dotmatrix_2 (.col0(out_15));
  LED led_30 (.in(register_2_q[2]));
  LED led_31 (.in(register_2_q[1]));
  LED led_32 (.in(register_2_q[0]));
  assign controlled_buffer_4_out = in_8 ? register_2_q : 8'bz;  // Controlled_Buffer controlled_buffer_4
  DotMatrix #(.dotshape("circle"), .matrixcols(1), .matrixrows(8)) dotmatrix_3 (.col0(register_1_q));
  assign and_1_out = register_2_q & register_1_q;  // AND_Gate and_1, 8 bits wide
  DotMatrix #(.dotshape("circle"), .matrixcols(1), .matrixrows(8)) dotmatrix_4 (.col0(register_2_q));
  DotMatrix #(.dotshape("circle"), .matrixcols(1), .matrixrows(8)) dotmatrix_5 (.col0(and_1_out));
  DotMatrix #(.dotshape("circle"), .matrixcols(1), .matrixrows(8)) dotmatrix_6 (.col0(not_1_out));
  assign not_1_out = ~and_1_out;  // NOT_Gate not_1, 8 bits wide
  assign or_1_out = register_2_q | register_1_q;  // OR_Gate or_1, 8 bits wide
  DotMatrix #(.dotshape("circle"), .matrixcols(1), .matrixrows(8)) dotmatrix_7 (.col0(or_1_out));
  DotMatrix #(.dotshape("circle"), .matrixcols(1), .matrixrows(8)) dotmatrix_8 (.col0(not_2_out));
  assign not_2_out = ~or_1_out;  // NOT_Gate not_2, 8 bits wide
  assign xor_1_out = register_2_q ^ register_1_q;  // XOR_Gate xor_1, 8 bits wide
  DotMatrix #(.dotshape("circle"), .matrixcols(1), .matrixrows(8)) dotmatrix_9 (.col0(xor_1_out));
  assign not_3_out = ~xor_1_out;  // NOT_Gate not_3, 8 bits wide
  assign controlled_buffer_5_out = bcd_to_7_segment_decoder_7_p3 ? d_ff_1_q : 8'bz;  // Controlled_Buffer controlled_buffer_5
  assign not_4_out = ~register_1_q;  // NOT_Gate not_4, 8 bits wide
  DotMatrix #(.dotshape("circle"), .matrixcols(1), .matrixrows(8)) dotmatrix_10 (.col0(not_3_out));
  DotMatrix #(.dotshape("circle"), .matrixcols(1), .matrixrows(8)) dotmatrix_11 (.col0(not_4_out));
  assign not_5_out = ~register_2_q;  // NOT_Gate not_5, 8 bits wide
  DotMatrix #(.dotshape("circle"), .matrixcols(1), .matrixrows(8)) dotmatrix_12 (.col0(not_5_out));
  D_Flip_Flop d_ff_1 (
    .D(undriven[0]), .clk(bcd_to_7_segment_decoder_7_p2), .Q(d_ff_1_q[0]),
    .reset(bcd_to_7_segment_decoder_7_p4));  // open: Qn, preset
  LED led_33 (.in(d_ff_1_q[0]));
  // _7_Segment_Display 7_segment_display_7: pin names not known; wires that end beside it: n7_segment_display_7_p1, n7_segment_display_7_p1
  // BCD_to_7_Segment_decoder bcd_to_7_segment_decoder_7: pin names not known; wires that end beside it: controlled_buffer_5_out, bcd_to_7_segment_decoder_7_p2, bcd_to_7_segment_decoder_7_p3, bcd_to_7_segment_decoder_7_p4
  D_Flip_Flop d_ff_2 (
    .D(undriven[1]), .clk(bcd_to_7_segment_decoder_7_p2), .Q(d_ff_1_q[1]),
    .reset(bcd_to_7_segment_decoder_7_p4));  // open: Qn, preset
  // _7_Segment_Display 7_segment_display_8: pin names not known; wires that end beside it: n7_segment_display_8_p1, n7_segment_display_8_p1
  // BCD_to_7_Segment_decoder bcd_to_7_segment_decoder_8: pin names not known
  // Binary_to_BCD_converter #(.binvalue(8)) binary_to_bcd_converter_3: pin names not known; wires that end beside it: binary_to_bcd_converter_3_p1, binary_to_bcd_converter_3_p1
  D_Flip_Flop d_ff_3 (
    .D(undriven[2]), .clk(bcd_to_7_segment_decoder_7_p2), .Q(d_ff_1_q[2]),
    .reset(bcd_to_7_segment_decoder_7_p4));  // open: Qn, preset
  LED led_34 (.in(d_ff_1_q[1]));
  // _7_Segment_Display 7_segment_display_9: pin names not known; wires that end beside it: n7_segment_display_9_p1, n7_segment_display_9_p1
  // BCD_to_7_Segment_decoder bcd_to_7_segment_decoder_9: pin names not known
  D_Flip_Flop d_ff_4 (
    .D(undriven[3]), .clk(bcd_to_7_segment_decoder_7_p2), .Q(d_ff_1_q[3]),
    .reset(bcd_to_7_segment_decoder_7_p4));  // open: Qn, preset
  LED led_35 ();  // open: in
  DotMatrix #(.dotshape("circle"), .inputtype("row"), .matrixcols(8), .matrixrows(1)) dotmatrix_13 ();  // open: row0
  LED led_36 (.in(undriven_3[7]));
  LED led_37 (.in(undriven_2[7]));
  LED led_38 (.in(d_ff_1_q[3]));
  LED led_39 (.in(undriven_3[6]));
  LED led_40 (.in(undriven_3[5]));
  LED led_41 (.in(undriven_3[4]));
  LED led_42 (.in(undriven_2[6]));
  LED led_43 (.in(undriven_2[5]));
  D_Flip_Flop d_ff_5 (
    .D(undriven[4]), .clk(bcd_to_7_segment_decoder_7_p2), .Q(d_ff_1_q[4]),
    .reset(bcd_to_7_segment_decoder_7_p4));  // open: Qn, preset
  LED led_44 (.in(d_ff_1_q[4]));
  LED led_45 (.in(undriven_3[3]));
  LED led_46 (.in(undriven_3[2]));
  LED led_47 (.in(undriven_2[4]));
  LED led_48 (.in(undriven_2[3]));
  LED led_49 (.in(undriven_2[2]));
  D_Flip_Flop d_ff_6 (
    .D(undriven[5]), .clk(bcd_to_7_segment_decoder_7_p2), .Q(d_ff_1_q[5]),
    .reset(bcd_to_7_segment_decoder_7_p4));  // open: Qn, preset
  LED led_50 (.in(undriven_3[1]));
  LED led_51 (.in(undriven_3[0]));
  LED led_52 (.in(undriven_2[1]));
  LED led_53 (.in(undriven_2[0]));
  D_Flip_Flop d_ff_7 (
    .D(undriven[6]), .clk(bcd_to_7_segment_decoder_7_p2), .Q(d_ff_1_q[6]),
    .reset(bcd_to_7_segment_decoder_7_p4));  // open: Qn, preset
  LED led_54 (.in(d_ff_1_q[5]));
  LED led_55 (.in(register_3_q[7]));
  LED led_56 (.in(register_3_q[6]));
  LED led_57 (.in(register_3_q[5]));
  D_Flip_Flop d_ff_8 (
    .D(undriven[7]), .clk(bcd_to_7_segment_decoder_7_p2), .Q(d_ff_1_q[7]),
    .reset(bcd_to_7_segment_decoder_7_p4));  // open: Qn, preset
  LED led_58 (.in(d_ff_1_q[6]));
  LED led_59 (.in(register_3_q[4]));
  LED led_60 (.in(register_3_q[3]));
  LED led_61 (.in(register_3_q[2]));
  Register register_3 (.D(controlled_buffer_6_out), .en(undriven_4), .clk(Clock), .Q(register_3_q), .clr(Reset));
  LED led_62 (.in(d_ff_1_q[7]));
  LED led_63 (.in(register_3_q[1]));
  LED led_64 (.in(register_3_q[0]));
  assign controlled_buffer_6_out = undriven_5 ? register_3_q : 8'bz;  // Controlled_Buffer controlled_buffer_6

  // Other names for the same wires on the sheet: A_In = in_5; A_Out = in_7; ALU_Instruction[3:0] = in_9; B_In = in_6;
  //   B_Out = in_8; Counter_Enable = in_4; Counter_In = in_2; Counter_Out = in_3
endmodule
