// Logisim project CPU1_v5.circ as structural Verilog: 1 circuit, main circuit main
module main (
  input  in_1,
  input  in_2,
  input  in_3,
  input  in_4,
  input  in_5,
  input  in_6,
  input  in_7,
  input  in_8,
  input  in_9,
  input  in_10,
  input  in_11,
  input  in_12,
  input  in_13,
  input  in_14,
  input  in_15,
  input  in_16,
  input  [3:0] in_17,
  output [1:0] out_18,
  output [1:0] out_19,
  output [3:0] out_20,
  output [1:0] out_21,
  output [7:0] out_22,
  output [7:0] out_23,
  output [7:0] _0100,
  output [7:0] out_25,
  output [15:0] out_26,
  output [7:0] _0001,
  output [7:0] _0011,
  output [3:0] Timestep,
  output [7:0] _0101,
  output [23:0] out_31,
  output [3:0] out_32,
  output [23:0] out_33
);

  wire adder_1_cout, and_1_out, and_3_out, bcd_to_7_segment_decoder_4_p2, bcd_to_7_segment_decoder_4_p3,
       bcd_to_7_segment_decoder_4_p4, binary_to_bcd_converter_2_p1, clock_1_out, comparator_1_gt,
       comparator_2_lt, comparator_3_gt, d_ff_1_qn, Main_Clock, multiplexer_2_out, n7_segment_display_1_p1,
       n7_segment_display_2_p1, n7_segment_display_3_p1, n7_segment_display_4_p1, n7_segment_display_5_p1,
       n7_segment_display_6_p1, not_1_out, not_2_out, not_3_out, not_4_out, or_1_out, Reset, undriven_4,
       undriven_5, undriven_6;
  wire [1:0] comparator_4_eq, multiplexer_1_out;
  wire [7:0] and_4_out, controlled_buffer_1_out, controlled_buffer_7_out, controlled_buffer_8_out,
       counter_2_q, d_ff_2_q, dipswitch_1_sw1, Memory_Addr_Reg_q, multiplier_1_cout, not_5_out, not_6_out,
       not_7_out, not_8_out, not_9_out, or_2_out, ram_1_dout, register_4_q, undriven, undriven_2, undriven_3,
       xor_1_out;

  Counter #(.max('hf), .width(4)) counter_1 (
    .clr(Reset), .load(in_14), .up(1'b1), .count(1'b1), .clk(Main_Clock), .D(4'b0000), .Q(Timestep));  // open: carry
  Button button_1 (.out(Reset));
  or or_1 (or_1_out, Reset, and_1_out);
  and and_1 (and_1_out, Main_Clock, in_14);
  Register Instr_Reg (.D(controlled_buffer_1_out), .en(in_11), .clk(Main_Clock), .Q(out_26[15:8]), .clr(or_1_out));
  ROM #(.addrWidth(12), .dataWidth(24)) Microcode (.addr({out_26[15:8], Timestep}), .data(out_31));
  D_Flip_Flop d_ff_1 (.D(in_15), .clk(Main_Clock), .Qn(d_ff_1_qn), .reset(Reset));  // open: Q, preset
  Register InstrData_Reg (.D(controlled_buffer_1_out), .en(in_12), .clk(Main_Clock), .Q(out_26[7:0]), .clr(or_1_out));
  Clock clock_1 (.out(clock_1_out));
  Register Memory_Addr_Reg (
    .D(controlled_buffer_1_out), .en(in_10), .clk(Main_Clock), .Q(Memory_Addr_Reg_q), .clr(Reset));
  DotMatrix #(.dotshape("circle"), .inputtype("row"), .matrixcols(8), .matrixrows(1)) dotmatrix_1 (.row0(out_26[15:8]));
  DotMatrix #(.dotshape("circle"), .inputtype("row"), .matrixcols(8), .matrixrows(1)) dotmatrix_2 (.row0(out_26[7:0]));
  LED led_1 (.in(clock_1_out));
  and and_2 (Main_Clock, clock_1_out, d_ff_1_qn);
  RAM #(.enables("line")) ram_1 (
    .addr(Memory_Addr_Reg_q), .we(in_8), .clk(Main_Clock), .din(controlled_buffer_1_out), .dout(ram_1_dout));
  assign controlled_buffer_1_out = in_13 ? out_26[7:0] : 8'bz;  // Controlled_Buffer controlled_buffer_1
  LED led_2 (.in(controlled_buffer_1_out[7]));
  DipSwitch dipswitch_1 (
    .sw1(dipswitch_1_sw1[0]), .sw2(dipswitch_1_sw1[1]), .sw3(dipswitch_1_sw1[2]), .sw4(dipswitch_1_sw1[3]),
    .sw5(dipswitch_1_sw1[4]), .sw6(dipswitch_1_sw1[5]), .sw7(dipswitch_1_sw1[6]), .sw8(dipswitch_1_sw1[7]));
  assign controlled_buffer_1_out = in_9 ? ram_1_dout : 8'bz;  // Controlled_Buffer controlled_buffer_2
  LED led_3 (.in(controlled_buffer_1_out[6]));
  LED led_4 (.in(controlled_buffer_1_out[5]));
  LED led_5 (.in(controlled_buffer_1_out[4]));
  LED led_6 (.in(controlled_buffer_1_out[3]));
  LED led_7 (.in(controlled_buffer_1_out[2]));
  LED led_8 (.in(controlled_buffer_1_out[1]));
  LED led_9 (.in(controlled_buffer_1_out[0]));
  Pull_Resistor pull_resistor_1 (.node(controlled_buffer_1_out));
  assign controlled_buffer_1_out = in_1 ? dipswitch_1_sw1 : 8'bz;  // Controlled_Buffer controlled_buffer_3
  // _7_Segment_Display 7_segment_display_1: pin names not known; wires that end beside it: n7_segment_display_1_p1, n7_segment_display_1_p1
  // BCD_to_7_Segment_decoder bcd_to_7_segment_decoder_1: pin names not known
  // Binary_to_BCD_converter #(.binvalue(8)) binary_to_bcd_converter_1: pin names not known; wires that end beside it: controlled_buffer_1_out
  Register #(.width(2)) register_1 (.D(multiplexer_1_out), .en(and_3_out), .clk(Main_Clock), .Q(out_18), .clr(Reset));
  // _7_Segment_Display 7_segment_display_2: pin names not known; wires that end beside it: n7_segment_display_2_p1, n7_segment_display_2_p1
  // BCD_to_7_Segment_decoder bcd_to_7_segment_decoder_2: pin names not known
  and and_3 (and_3_out, comparator_2_lt, comparator_1_gt);
  Comparator #(.mode("unsigned"), .width(4)) comparator_1 (
    .a(out_32), .b(4'b0000), .gt(comparator_1_gt));  // open: eq, lt
  // _7_Segment_Display 7_segment_display_3: pin names not known; wires that end beside it: n7_segment_display_3_p1, n7_segment_display_3_p1
  // BCD_to_7_Segment_decoder bcd_to_7_segment_decoder_3: pin names not known
  Multiplexer #(.enable("false"), .select(2)) multiplexer_1 (
    .in0(1'b0), .in1(adder_1_cout), .in2(1'b0), .in3(comparator_3_gt), .out(multiplexer_1_out[0]),
    .sel(out_32[1:0]));
  Comparator #(.mode("unsigned"), .width(4)) comparator_2 (
    .a(out_32), .b(4'b0100), .lt(comparator_2_lt));  // open: gt, eq
  Adder adder_1 (.a(out_22), .b(out_23), .out(_0001), .cout(adder_1_cout));  // open: cin
  Counter counter_2 (
    .clr(Reset), .load(multiplexer_2_out), .up(1'b1), .count(in_3), .clk(Main_Clock),
    .D(controlled_buffer_1_out), .Q(counter_2_q));  // open: carry
  LED led_10 (.in(out_22[7]));
  LED led_11 (.in(out_22[6]));
  LED led_12 (.in(out_22[5]));
  Subtractor subtractor_1 (.a(out_22), .b(out_23), .out(_0011), .bout(multiplexer_1_out[1]));  // open: bin
  LED led_13 (.in(out_22[4]));
  LED led_14 (.in(out_22[3]));
  LED led_15 (.in(out_22[2]));
  LED led_16 (.in(out_22[1]));
  Register register_2 (.D(controlled_buffer_1_out), .en(in_4), .clk(Main_Clock), .Q(out_22), .clr(Reset));
  Comparator #(.mode("unsigned")) comparator_3 (
    .a(multiplier_1_cout), .b({8{1'b0}}), .gt(comparator_3_gt));  // open: eq, lt
  not not_1 (not_1_out, out_19[0]);
  assign controlled_buffer_1_out = in_2 ? counter_2_q : 8'bz;  // Controlled_Buffer controlled_buffer_4
  LED led_17 (.in(out_22[0]));
  assign controlled_buffer_1_out = in_5 ? out_22 : 8'bz;  // Controlled_Buffer controlled_buffer_5
  Multiplier multiplier_1 (.a(out_22), .b(out_23), .out(_0100), .cout(multiplier_1_cout));  // open: cin
  Pull_Resistor pull_resistor_2 (.node(out_33[18]));
  Demultiplexer #(.enable("false"), .width(4)) demultiplexer_1 (.out0(out_32), .out1(out_20), .in(in_17), .sel(in_16));
  not not_2 (not_2_out, out_18[1]);
  not not_3 (not_3_out, out_18[0]);
  not not_4 (not_4_out, out_19[1]);
  Multiplexer #(.enable("false"), .select(4)) multiplexer_2 (
    .in0(1'b0), .in1(1'b1), .in2(out_19[0]), .in3(not_1_out), .in4(out_19[1]), .in5(not_4_out),
    .in6(out_18[1]), .in7(not_2_out), .in8(out_18[0]), .in9(not_3_out), .in10(1'b0), .in11(1'b0),
    .in12(1'b0), .in13(1'b0), .in14(1'b0), .in15(1'b0), .out(multiplexer_2_out), .sel(out_20));
  LED led_18 (.in(out_23[7]));
  LED led_19 (.in(out_23[6]));
  Divider divider_1 (.a(out_22), .b(out_23), .out(out_25), .rem(_0101));  // open: upper
  LED led_20 (.in(out_23[5]));
  LED led_21 (.in(out_23[4]));
  LED led_22 (.in(out_23[3]));
  LED led_23 (.in(out_23[2]));
  Register register_3 (.D(controlled_buffer_1_out), .en(in_6), .clk(Main_Clock), .Q(out_23), .clr(Reset));
  Multiplexer #(.enable("false"), .select(4), .width(8)) multiplexer_3 (
    .in1(_0001), .in2(_0011), .in3(_0100), .in4(out_25), .in5(_0101), .in6(and_4_out), .in7(not_5_out),
    .in8(or_2_out), .in9(not_6_out), .in10(xor_1_out), .in11(not_7_out), .in12(not_8_out), .in13(not_9_out),
    .out(controlled_buffer_1_out), .sel(out_32));  // open: in0, in14, in15
  LED led_24 (.in(out_23[1]));
  LED led_25 (.in(out_23[0]));
  assign controlled_buffer_1_out = in_7 ? out_23 : 8'bz;  // Controlled_Buffer controlled_buffer_6
  DotMatrix #(.dotshape("circle"), .matrixcols(1), .matrixrows(8)) dotmatrix_3 (.col0(out_22));
  DotMatrix #(.dotshape("circle"), .matrixcols(1), .matrixrows(8)) dotmatrix_4 (.col0(out_23));
  assign and_4_out = out_23 & out_22;  // AND_Gate and_4, 8 bits wide
  assign not_5_out = ~and_4_out;  // NOT_Gate not_5, 8 bits wide
  Comparator #(.mode("unsigned")) comparator_4 (.a(out_22), .b({8{1'b0}}), .eq(comparator_4_eq[0]));  // open: gt, lt
  Register #(.width(2)) Reg_Zflags (.D(comparator_4_eq), .en(1'b1), .clk(Main_Clock), .Q(out_19), .clr(1'b0));
  Comparator #(.mode("unsigned")) comparator_5 (.a(out_23), .b({8{1'b0}}), .eq(comparator_4_eq[1]));  // open: gt, lt
  assign or_2_out = out_23 | out_22;  // OR_Gate or_2, 8 bits wide
  DotMatrix #(.dotshape("circle"), .matrixcols(1), .matrixrows(8)) dotmatrix_5 (.col0(and_4_out));
  DotMatrix #(.dotshape("circle"), .matrixcols(1), .matrixrows(8)) dotmatrix_6 (.col0(not_5_out));
  assign not_6_out = ~or_2_out;  // NOT_Gate not_6, 8 bits wide
  DotMatrix #(.dotshape("circle"), .matrixcols(1), .matrixrows(8)) dotmatrix_7 (.col0(or_2_out));
  DotMatrix #(.dotshape("circle"), .matrixcols(1), .matrixrows(8)) dotmatrix_8 (.col0(not_6_out));
  assign xor_1_out = out_23 ^ out_22;  // XOR_Gate xor_1, 8 bits wide
  DotMatrix #(.dotshape("circle"), .matrixcols(1), .matrixrows(8)) dotmatrix_9 (.col0(xor_1_out));
  DotMatrix #(.dotshape("circle"), .matrixcols(1), .matrixrows(8)) dotmatrix_10 (.col0(not_7_out));
  assign not_7_out = ~xor_1_out;  // NOT_Gate not_7, 8 bits wide
  assign not_8_out = ~out_22;  // NOT_Gate not_8, 8 bits wide
  assign not_9_out = ~out_23;  // NOT_Gate not_9, 8 bits wide
  DotMatrix #(.dotshape("circle"), .matrixcols(1), .matrixrows(8)) dotmatrix_11 (.col0(not_8_out));
  DotMatrix #(.dotshape("circle"), .matrixcols(1), .matrixrows(8)) dotmatrix_12 (.col0(not_9_out));
  assign controlled_buffer_7_out = bcd_to_7_segment_decoder_4_p3 ? d_ff_2_q : 8'bz;  // Controlled_Buffer controlled_buffer_7
  D_Flip_Flop d_ff_2 (
    .D(undriven[0]), .clk(bcd_to_7_segment_decoder_4_p2), .Q(d_ff_2_q[0]),
    .reset(bcd_to_7_segment_decoder_4_p4));  // open: Qn, preset
  LED led_26 (.in(d_ff_2_q[0]));
  // _7_Segment_Display 7_segment_display_4: pin names not known; wires that end beside it: n7_segment_display_4_p1, n7_segment_display_4_p1
  // BCD_to_7_Segment_decoder bcd_to_7_segment_decoder_4: pin names not known; wires that end beside it: controlled_buffer_7_out, bcd_to_7_segment_decoder_4_p2, bcd_to_7_segment_decoder_4_p3, bcd_to_7_segment_decoder_4_p4
  D_Flip_Flop d_ff_3 (
    .D(undriven[1]), .clk(bcd_to_7_segment_decoder_4_p2), .Q(d_ff_2_q[1]),
    .reset(bcd_to_7_segment_decoder_4_p4));  // open: Qn, preset
  // _7_Segment_Display 7_segment_display_5: pin names not known; wires that end beside it: n7_segment_display_5_p1, n7_segment_display_5_p1
  // BCD_to_7_Segment_decoder bcd_to_7_segment_decoder_5: pin names not known
  // Binary_to_BCD_converter #(.binvalue(8)) binary_to_bcd_converter_2: pin names not known; wires that end beside it: binary_to_bcd_converter_2_p1, binary_to_bcd_converter_2_p1
  D_Flip_Flop d_ff_4 (
    .D(undriven[2]), .clk(bcd_to_7_segment_decoder_4_p2), .Q(d_ff_2_q[2]),
    .reset(bcd_to_7_segment_decoder_4_p4));  // open: Qn, preset
  LED led_27 (.in(d_ff_2_q[1]));
  // _7_Segment_Display 7_segment_display_6: pin names not known; wires that end beside it: n7_segment_display_6_p1, n7_segment_display_6_p1
  // BCD_to_7_Segment_decoder bcd_to_7_segment_decoder_6: pin names not known
  D_Flip_Flop d_ff_5 (
    .D(undriven[3]), .clk(bcd_to_7_segment_decoder_4_p2), .Q(d_ff_2_q[3]),
    .reset(bcd_to_7_segment_decoder_4_p4));  // open: Qn, preset
  LED led_28 ();  // open: in
  DotMatrix #(.dotshape("circle"), .inputtype("row"), .matrixcols(8), .matrixrows(1)) dotmatrix_13 ();  // open: row0
  LED led_29 (.in(undriven_3[7]));
  LED led_30 (.in(undriven_2[7]));
  LED led_31 (.in(d_ff_2_q[3]));
  LED led_32 (.in(undriven_3[6]));
  LED led_33 (.in(undriven_3[5]));
  LED led_34 (.in(undriven_3[4]));
  LED led_35 (.in(undriven_2[6]));
  LED led_36 (.in(undriven_2[5]));
  D_Flip_Flop d_ff_6 (
    .D(undriven[4]), .clk(bcd_to_7_segment_decoder_4_p2), .Q(d_ff_2_q[4]),
    .reset(bcd_to_7_segment_decoder_4_p4));  // open: Qn, preset
  LED led_37 (.in(d_ff_2_q[4]));
  LED led_38 (.in(undriven_3[3]));
  LED led_39 (.in(undriven_3[2]));
  LED led_40 (.in(undriven_2[4]));
  LED led_41 (.in(undriven_2[3]));
  LED led_42 (.in(undriven_2[2]));
  D_Flip_Flop d_ff_7 (
    .D(undriven[5]), .clk(bcd_to_7_segment_decoder_4_p2), .Q(d_ff_2_q[5]),
    .reset(bcd_to_7_segment_decoder_4_p4));  // open: Qn, preset
  LED led_43 (.in(undriven_3[1]));
  LED led_44 (.in(undriven_3[0]));
  LED led_45 (.in(undriven_2[1]));
  LED led_46 (.in(undriven_2[0]));
  D_Flip_Flop d_ff_8 (
    .D(undriven[6]), .clk(bcd_to_7_segment_decoder_4_p2), .Q(d_ff_2_q[6]),
    .reset(bcd_to_7_segment_decoder_4_p4));  // open: Qn, preset
  LED led_47 (.in(d_ff_2_q[5]));
  LED led_48 (.in(register_4_q[7]));
  LED led_49 (.in(register_4_q[6]));
  LED led_50 (.in(register_4_q[5]));
  D_Flip_Flop d_ff_9 (
    .D(undriven[7]), .clk(bcd_to_7_segment_decoder_4_p2), .Q(d_ff_2_q[7]),
    .reset(bcd_to_7_segment_decoder_4_p4));  // open: Qn, preset
  LED led_51 (.in(d_ff_2_q[6]));
  LED led_52 (.in(register_4_q[4]));
  LED led_53 (.in(register_4_q[3]));
  LED led_54 (.in(register_4_q[2]));
  Register register_4 (.D(controlled_buffer_8_out), .en(undriven_4), .clk(undriven_5), .Q(register_4_q), .clr(Reset));
  LED led_55 (.in(d_ff_2_q[7]));
  LED led_56 (.in(register_4_q[1]));
  LED led_57 (.in(register_4_q[0]));
  assign controlled_buffer_8_out = undriven_6 ? register_4_q : 8'bz;  // Controlled_Buffer controlled_buffer_8

  assign out_21 = out_19;
  assign {out_33[23:19], out_33[17:0]} = {in_17, in_16, {4{out_33[18]}}, in_15, in_14, in_13, in_12, in_11, in_10, in_9, in_8, in_7, in_6, in_5, in_4, in_3, in_2};

  // Other names for the same wires on the sheet: ALU_CW[3:0] = out_32; ALU_Flags[1:0] = out_18; JMP_CW[3:0] = out_20;
  //   Counter_Out = in_2; Counter_Enable = in_3; A_In = in_4; A_Out = in_5; B_In = in_6; B_Out = in_7; Mem_In = in_8;
  //   Mem_Out = in_9; MAR_In = in_10; IR_In = in_11; IDR_In = in_12; IDR_Out = in_13; Instr_Reset = in_14;
  //   Halt = in_15; Reg_ZFlags[1:0] = out_19

  // Notes on the sheet:
  //   Instruction
  //   Controlword
  //   Register A
  //   Register B
  //   0010
  //   A
  //   B
  //   0110, inv 0111
  //   1000, inv 1001
  //   1010, inv 1011
  //   No reset needed, automatically resets 1 cp after registers are reset
  //   1100
  //   1101
endmodule
