// Logisim project CPU1_v6.circ as structural Verilog: 1 circuit, main circuit main
module main (
  output [1:0] out_1,
  output [1:0] out_2,
  output [31:0] Cycle_count,
  output [3:0] out_4,
  output [7:0] out_5,
  output [7:0] out_6,
  output [7:0] out_7,
  output [7:0] out_8,
  output [7:0] _0100,
  output [7:0] out_10,
  output [15:0] out_11,
  output [7:0] _0001,
  output [7:0] _0011,
  output [3:0] Timestep,
  output [7:0] _0101,
  output [23:0] out_16,
  output out_17,
  output out_18,
  output out_19,
  output out_20,
  output [3:0] out_21,
  output out_22,
  output out_23,
  output out_24,
  output out_25,
  output out_26,
  output out_27,
  output out_28,
  output out_29,
  output out_30,
  output out_31,
  output out_32,
  output [3:0] out_33,
  output [3:0] out_34
);

  wire adder_1_cout, and_1_out, and_3_out, binary_to_bcd_converter_2_p1, clock_1_out, comparator_1_gt,
       comparator_2_lt, comparator_3_gt, d_ff_1_qn, Main_Clock, multiplexer_2_out, n7_segment_display_1_p1,
       n7_segment_display_2_p1, n7_segment_display_3_p1, n7_segment_display_4_p1, n7_segment_display_5_p1,
       n7_segment_display_6_p1, not_1_out, not_2_out, not_3_out, not_4_out, or_1_out, or_2_out, Reset;
  wire [1:0] multiplexer_1_out;
  wire [7:0] and_4_out, counter_3_q, Memory_Addr_Reg_q, multiplier_1_cout, not_5_out, not_6_out, not_7_out,
       not_8_out, not_9_out, or_3_out, ram_1_dout, register_1_q, undriven, undriven_2, xor_1_out;

  Counter #(.max('hf), .width(4)) counter_1 (
    .clr(or_1_out), .load(1'b0), .up(1'b1), .count(1'b1), .clk(Main_Clock), .Q(Timestep));  // open: D, carry
  or or_1 (or_1_out, out_16[12], Reset);
  or or_2 (or_2_out, Reset, and_1_out);
  and and_1 (and_1_out, out_16[12], Main_Clock);
  Register Instr_Reg (.D(out_5), .en(out_16[9]), .clk(Main_Clock), .Q(out_11[15:8]), .clr(or_2_out));
  ROM #(.addrWidth(12), .dataWidth(24)) Microcode (.addr({out_11[15:8], Timestep}), .data(out_16));
  Register InstrData_Reg (.D(out_5), .en(out_16[10]), .clk(Main_Clock), .Q(out_11[7:0]), .clr(or_2_out));
  Register Memory_Addr_Reg (.D(out_5), .en(out_16[8]), .clk(Main_Clock), .Q(Memory_Addr_Reg_q), .clr(Reset));
  Register register_1 (.D(out_5), .en(out_16[14]), .clk(Main_Clock), .Q(register_1_q), .clr(Reset));
  RAM #(.enables("line")) ram_1 (
    .addr(Memory_Addr_Reg_q), .we(out_16[6]), .clk(Main_Clock), .din(out_5), .dout(ram_1_dout));
  assign out_5 = out_16[11] ? out_11[7:0] : 8'bz;  // Controlled_Buffer controlled_buffer_1
  DotMatrix #(.inputtype("row"), .matrixcols(8), .matrixrows(2)) dotmatrix_1 (.row0(out_11[15:8]), .row1(out_11[7:0]));
  Demultiplexer #(.enable("false"), .width(4)) demultiplexer_1 (
    .out0(out_21), .out1(out_4), .in(out_16[23:20]), .sel(out_16[19]));
  // _7_Segment_Display 7_segment_display_1: pin names not known; wires that end beside it: n7_segment_display_1_p1, n7_segment_display_1_p1
  // BCD_to_7_Segment_decoder bcd_to_7_segment_decoder_1: pin names not known
  // Binary_to_BCD_converter #(.binvalue(8)) binary_to_bcd_converter_1: pin names not known; wires that end beside it: register_1_q
  // _7_Segment_Display 7_segment_display_2: pin names not known; wires that end beside it: n7_segment_display_2_p1, n7_segment_display_2_p1
  // _7_Segment_Display 7_segment_display_3: pin names not known; wires that end beside it: n7_segment_display_3_p1, n7_segment_display_3_p1
  // BCD_to_7_Segment_decoder bcd_to_7_segment_decoder_2: pin names not known
  // BCD_to_7_Segment_decoder bcd_to_7_segment_decoder_3: pin names not known
  assign out_5 = out_16[7] ? ram_1_dout : 8'bz;  // Controlled_Buffer controlled_buffer_2
  Button button_1 (.out(Reset));
  Clock clock_1 (.out(clock_1_out));
  D_Flip_Flop d_ff_1 (.D(out_16[13]), .clk(Main_Clock), .Qn(d_ff_1_qn), .reset(Reset));  // open: Q, preset
  Pull_Resistor pull_resistor_1 (.node(out_5));
  and and_2 (Main_Clock, clock_1_out, d_ff_1_qn);
  Register #(.width(2)) register_2 (.D(multiplexer_1_out), .en(and_3_out), .clk(Main_Clock), .Q(out_1), .clr(Reset));
  Counter #(.max('hffffffff), .width(32)) counter_2 (
    .load(1'b0), .count(1'b1), .Q(Cycle_count), .up(1'b1), .clk(Main_Clock), .clr(Reset));  // open: D, carry
  and and_3 (and_3_out, comparator_2_lt, comparator_1_gt);
  Comparator #(.mode("unsigned"), .width(4)) comparator_1 (
    .a(out_21), .b(4'b0000), .gt(comparator_1_gt));  // open: eq, lt
  Multiplexer #(.enable("false"), .select(2)) multiplexer_1 (
    .in0(1'b0), .in1(adder_1_cout), .in2(1'b0), .in3(comparator_3_gt), .out(multiplexer_1_out[0]),
    .sel(out_21[1:0]));
  Comparator #(.mode("unsigned"), .width(4)) comparator_2 (
    .a(out_21), .b(4'b0100), .lt(comparator_2_lt));  // open: gt, eq
  Adder adder_1 (.a(out_7), .b(out_8), .out(_0001), .cout(adder_1_cout));  // open: cin
  Counter counter_3 (
    .clr(Reset), .load(multiplexer_2_out), .up(1'b1), .count(out_16[1]), .clk(Main_Clock), .D(out_5),
    .Q(counter_3_q));  // open: carry
  LED led_1 (.in(out_7[7]));
  LED led_2 (.in(out_7[6]));
  LED led_3 (.in(out_7[5]));
  Subtractor subtractor_1 (.a(out_7), .b(out_8), .out(_0011), .bout(multiplexer_1_out[1]));  // open: bin
  LED led_4 (.in(out_7[4]));
  LED led_5 (.in(out_7[3]));
  LED led_6 (.in(out_7[2]));
  LED led_7 (.in(out_7[1]));
  Register register_3 (.D(out_5), .en(out_16[2]), .clk(Main_Clock), .Q(out_7), .clr(Reset));
  Comparator #(.mode("unsigned")) comparator_3 (
    .a(multiplier_1_cout), .b({8{1'b0}}), .gt(comparator_3_gt));  // open: eq, lt
  not not_1 (not_1_out, out_2[0]);
  assign out_5 = out_16[0] ? counter_3_q : 8'bz;  // Controlled_Buffer controlled_buffer_3
  LED led_8 (.in(out_7[0]));
  assign out_5 = out_16[3] ? out_7 : 8'bz;  // Controlled_Buffer controlled_buffer_4
  Multiplier multiplier_1 (.a(out_7), .b(out_8), .out(_0100), .cout(multiplier_1_cout));  // open: cin
  not not_2 (not_2_out, out_1[1]);
  not not_3 (not_3_out, out_1[0]);
  not not_4 (not_4_out, out_2[1]);
  Multiplexer #(.enable("false"), .select(4)) multiplexer_2 (
    .in0(1'b0), .in1(1'b1), .in2(out_2[0]), .in3(not_1_out), .in4(out_2[1]), .in5(not_4_out), .in6(out_1[1]),
    .in7(not_2_out), .in8(out_1[0]), .in9(not_3_out), .in10(1'b0), .in11(1'b0), .in12(1'b0), .in13(1'b0),
    .in14(1'b0), .in15(1'b0), .out(multiplexer_2_out), .sel(out_4));
  LED led_9 (.in(out_8[7]));
  LED led_10 (.in(out_8[6]));
  Divider divider_1 (.a(out_7), .b(out_8), .out(out_10), .rem(_0101));  // open: upper
  LED led_11 (.in(out_8[5]));
  LED led_12 (.in(out_8[4]));
  LED led_13 (.in(out_8[3]));
  LED led_14 (.in(out_8[2]));
  Register register_4 (.D(out_5), .en(out_16[4]), .clk(Main_Clock), .Q(out_8), .clr(Reset));
  Multiplexer #(.enable("false"), .select(4), .width(8)) multiplexer_3 (
    .in1(_0001), .in2(_0011), .in3(_0100), .in4(out_10), .in5(_0101), .in6(and_4_out), .in7(not_5_out),
    .in8(or_3_out), .in9(not_6_out), .in10(xor_1_out), .in11(not_7_out), .in12(not_8_out), .in13(not_9_out),
    .out(out_5), .sel(out_21));  // open: in0, in14, in15
  LED led_15 (.in(out_8[1]));
  LED led_16 (.in(out_8[0]));
  assign out_5 = out_16[5] ? out_8 : 8'bz;  // Controlled_Buffer controlled_buffer_5
  DotMatrix #(.dotshape("circle"), .matrixcols(1), .matrixrows(8)) dotmatrix_2 (.col0(out_7));
  DotMatrix #(.dotshape("circle"), .matrixcols(1), .matrixrows(8)) dotmatrix_3 (.col0(out_8));
  assign and_4_out = out_8 & out_7;  // AND_Gate and_4, 8 bits wide
  assign not_5_out = ~and_4_out;  // NOT_Gate not_5, 8 bits wide
  Comparator #(.mode("unsigned")) comparator_4 (.a(out_7), .b({8{1'b0}}), .eq(out_2[0]));  // open: gt, lt
  Comparator #(.mode("unsigned")) comparator_5 (.a(out_8), .b({8{1'b0}}), .eq(out_2[1]));  // open: gt, lt
  assign or_3_out = out_8 | out_7;  // OR_Gate or_3, 8 bits wide
  DotMatrix #(.dotshape("circle"), .matrixcols(1), .matrixrows(8)) dotmatrix_4 (.col0(and_4_out));
  DotMatrix #(.dotshape("circle"), .matrixcols(1), .matrixrows(8)) dotmatrix_5 (.col0(not_5_out));
  assign not_6_out = ~or_3_out;  // NOT_Gate not_6, 8 bits wide
  DotMatrix #(.dotshape("circle"), .matrixcols(1), .matrixrows(8)) dotmatrix_6 (.col0(or_3_out));
  DotMatrix #(.dotshape("circle"), .matrixcols(1), .matrixrows(8)) dotmatrix_7 (.col0(not_6_out));
  assign xor_1_out = out_8 ^ out_7;  // XOR_Gate xor_1, 8 bits wide
  DotMatrix #(.dotshape("circle"), .matrixcols(1), .matrixrows(8)) dotmatrix_8 (.col0(xor_1_out));
  DotMatrix #(.dotshape("circle"), .matrixcols(1), .matrixrows(8)) dotmatrix_9 (.col0(not_7_out));
  assign not_7_out = ~xor_1_out;  // NOT_Gate not_7, 8 bits wide
  assign not_8_out = ~out_7;  // NOT_Gate not_8, 8 bits wide
  assign not_9_out = ~out_8;  // NOT_Gate not_9, 8 bits wide
  DotMatrix #(.dotshape("circle"), .matrixcols(1), .matrixrows(8)) dotmatrix_10 (.col0(not_8_out));
  DotMatrix #(.dotshape("circle"), .matrixcols(1), .matrixrows(8)) dotmatrix_11 (.col0(not_9_out));
  // _7_Segment_Display 7_segment_display_4: pin names not known; wires that end beside it: n7_segment_display_4_p1, n7_segment_display_4_p1
  // BCD_to_7_Segment_decoder bcd_to_7_segment_decoder_4: pin names not known
  // _7_Segment_Display 7_segment_display_5: pin names not known; wires that end beside it: n7_segment_display_5_p1, n7_segment_display_5_p1
  // BCD_to_7_Segment_decoder bcd_to_7_segment_decoder_5: pin names not known
  // Binary_to_BCD_converter #(.binvalue(8)) binary_to_bcd_converter_2: pin names not known; wires that end beside it: binary_to_bcd_converter_2_p1, binary_to_bcd_converter_2_p1
  // _7_Segment_Display 7_segment_display_6: pin names not known; wires that end beside it: n7_segment_display_6_p1, n7_segment_display_6_p1
  // BCD_to_7_Segment_decoder bcd_to_7_segment_decoder_6: pin names not known
  DotMatrix #(.dotshape("circle"), .inputtype("row"), .matrixcols(8), .matrixrows(1)) dotmatrix_12 ();  // open: row0
  LED led_17 (.in(undriven_2[7]));
  LED led_18 (.in(undriven[7]));
  LED led_19 (.in(undriven_2[6]));
  LED led_20 (.in(undriven_2[5]));
  LED led_21 (.in(undriven_2[4]));
  LED led_22 (.in(undriven[6]));
  LED led_23 (.in(undriven[5]));
  LED led_24 (.in(undriven_2[3]));
  LED led_25 (.in(undriven_2[2]));
  LED led_26 (.in(undriven[4]));
  LED led_27 (.in(undriven[3]));
  LED led_28 (.in(undriven[2]));
  LED led_29 (.in(undriven_2[1]));
  LED led_30 (.in(undriven_2[0]));
  LED led_31 (.in(undriven[1]));
  LED led_32 (.in(undriven[0]));

  assign out_6 = out_5;
  assign out_17 = out_16[0];
  assign out_18 = out_16[1];
  assign out_19 = out_16[2];
  assign out_20 = out_16[3];
  assign out_22 = out_16[4];
  assign out_23 = out_16[5];
  assign out_24 = out_16[6];
  assign out_25 = out_16[7];
  assign out_26 = out_16[8];
  assign out_27 = out_16[9];
  assign out_28 = out_16[10];
  assign out_29 = out_16[11];
  assign out_30 = out_16[12];
  assign out_31 = out_16[13];
  assign out_32 = out_16[14];
  assign out_33 = out_21;
  assign out_34 = out_4;

  // Other names for the same wires on the sheet: ALU_CW[3:0] = out_21; ALU_Flags[1:0] = out_1; JMP_CW[3:0] = out_4;
  //   Counter_Out = out_16[0]; Counter_Enable = out_16[1]; A_In = out_16[2]; A_Out = out_16[3]; B_In = out_16[4];
  //   B_Out = out_16[5]; Mem_In = out_16[6]; Mem_Out = out_16[7]; MAR_In = out_16[8]; IR_In = out_16[9];
  //   IDR_In = out_16[10]; IDR_Out = out_16[11]; Instr_Reset = out_16[12]; Halt = out_16[13]; Out_In = out_16[14];
  //   Reg_ZFlags[1:0] = out_2

  // Notes on the sheet:
  //   contents of Microcode (hex, n*v repeats v):
  //   101 282 1000 15*0 101 482 804 1000 12*0 101 482 810 1000 12*0 101 482 900 84 1000 11*0 101 482 900
  //   90 1000 11*0 101 482 900 48 1000 11*0 101 482 900 90 100004 1000 10*0 101 482 810 100004 1000 11*0
  //   101 482 900 90 200004 1000 10*0 101 482 810 200004 1000 11*0 101 482 900 90 300004 1000 10*0 101 482
  //   810 300004 1000 11*0 101 482 900 90 400004 1000 10*0 101 482 810 400004 1000 11*0 101 482 900 90
  //   500004 1000 10*0 101 482 810 500004 1000 11*0 101 482 900 600040 1000 11*0 101 482 900 700040 1000
  //   11*0 101 482 900 800040 1000 11*0 101 482 900 900040 1000 11*0 101 482 900 a00040 1000 11*0 101 482
  //   900 b00040 1000 11*0 101 482 900 c00040 1000 11*0 101 482 900 d00040 1000 11*0 101 482 180800 1000
  //   12*0 101 482 280800 1000 12*0 101 482 380800 1000 12*0 101 482 480800 1000 12*0 101 482 580800 1000
  //   12*0 101 482 680800 1000 12*0 101 482 780800 1000 12*0 101 482 880800 1000 12*0 101 482 980800 1000
  //   12*0 2000 1000 14*0 4008 1000 14*0 101 482 900 4040 1000
  //   Instruction
  //   Controlword
  //   Register A
  //   Register B
  //   0010
  //   A
  //   B
  //   0110, inv 0111
  //   1000, inv 1001
  //   1010, inv 1011
  //   1100
  //   1101
endmodule
