// Logisim project CPU2_v1.circ as structural Verilog: 1 circuit, main circuit main
module main (
  input  in_1,
  input  [15:0] in_2,
  output [1:0] out_3,
  output [31:0] Cycle_count,
  output [3:0] out_5,
  output [15:0] out_6,
  output [15:0] out_7,
  output [15:0] out_8,
  output [15:0] out_9,
  output [15:0] out_10,
  output [15:0] out_11,
  output [15:0] out_12,
  output [15:0] out_13,
  output [15:0] out_14,
  output [15:0] out_15,
  output [15:0] out_16,
  output [15:0] out_17,
  output [15:0] out_18,
  output [15:0] out_19,
  output [15:0] out_20,
  output [15:0] out_21,
  output out_22,
  output [15:0] out_23,
  output [15:0] out_24,
  output [15:0] out_25,
  output [15:0] _0100,
  output [31:0] out_27,
  output [15:0] out_28,
  output [15:0] out_29,
  output [3:0] out_30,
  output [15:0] _0101,
  output [23:0] out_32,
  output out_33,
  output out_34,
  output out_35,
  output out_36,
  output [3:0] out_37,
  output out_38,
  output out_39,
  output out_40,
  output out_41,
  output out_42,
  output out_43,
  output out_44,
  output out_45,
  output out_46,
  output out_47,
  output out_48,
  output [3:0] out_49,
  output [3:0] out_50
);

  wire adder_1_cout, and_1_out, and_2_out, and_3_out, clock_1_out, comparator_1_gt, comparator_2_gt,
       comparator_3_lt, comparator_4_gt, d_ff_2_qn, Main_Clock, multiplexer_2_out, not_1_out, not_2_out,
       not_3_out, or_1_out, Reset;
  wire [1:0] multiplexer_1_out;
  wire [15:0] controlled_buffer_1_out, counter_2_q, Memory_Addr_Reg_q, multiplier_1_cout, ram_1_dout;

  Counter #(.max('hf), .width(4)) counter_1 (
    .load(1'b0), .up(1'b1), .count(1'b1), .clk(Main_Clock), .D(4'b0000), .Q(out_30));  // open: clr, carry
  RAM #(.addrWidth(16), .dataWidth(16), .enables("line")) ram_1 (
    .addr(Memory_Addr_Reg_q), .we(out_32[6]), .clk(Main_Clock), .din(controlled_buffer_1_out),
    .dout(ram_1_dout));
  or or_1 (or_1_out, Reset, and_1_out);
  and and_1 (and_1_out, out_32[12], Main_Clock);
  Register #(.width(16)) Instr_Reg (
    .D(controlled_buffer_1_out), .en(out_32[9]), .clk(Main_Clock), .Q(out_27[31:16]), .clr(or_1_out));
  ROM #(.addrWidth(20), .dataWidth(24)) Microcode (.addr({out_27[31:16], out_30}), .data(out_32));
  assign controlled_buffer_1_out = out_32[7] ? ram_1_dout : 16'bz;  // Controlled_Buffer controlled_buffer_1
  Register #(.width(16)) InstrData_Reg (
    .D(controlled_buffer_1_out), .en(out_32[10]), .clk(Main_Clock), .Q(out_27[15:0]), .clr(or_1_out));
  Register #(.width(16)) Memory_Addr_Reg (
    .D(controlled_buffer_1_out), .en(out_32[8]), .clk(Main_Clock), .Q(Memory_Addr_Reg_q), .clr(Reset));
  assign controlled_buffer_1_out = out_32[11] ? out_27[15:0] : 16'bz;  // Controlled_Buffer controlled_buffer_2
  DotMatrix #(.dotshape("circle"), .inputtype("row"), .matrixcols(16), .matrixrows(2)) dotmatrix_1 (
    .row0(out_27[31:16]), .row1(out_27[15:0]));
  DotMatrix #(.inputtype("row"), .matrixcols(24), .matrixrows(1)) dotmatrix_2 (.row0(out_32));
  Demultiplexer #(.enable("false"), .width(4)) demultiplexer_1 (
    .out0(out_37), .out1(out_5), .in(out_32[23:20]), .sel(out_32[19]));
  Button button_1 (.out(Reset));
  DotMatrix #(.dotshape("circle"), .inputtype("row"), .matrixcols(16), .matrixrows(1)) dotmatrix_3 (.row0(controlled_buffer_1_out));
  // Shift_Register #(.length(16), .width(16)) shift_register_1: pin names not known; wires that end beside it: Reset, 1'b0, out_32[14], Main_Clock, controlled_buffer_1_out, out_6, out_7, out_8, out_9, out_10, out_11, out_12, out_13, out_14, out_15, out_16, out_17
  Pull_Resistor pull_resistor_1 (.node(controlled_buffer_1_out));
  assign controlled_buffer_1_out = in_1 ? in_2 : 16'bz;  // Controlled_Buffer controlled_buffer_3
  Register #(.width(2)) register_1 (.D(multiplexer_1_out), .en(and_2_out), .clk(Main_Clock), .Q(out_3), .clr(Reset));
  Comparator #(.mode("unsigned"), .width(16)) comparator_1 (
    .a(controlled_buffer_1_out), .b({16{1'b0}}), .gt(comparator_1_gt));  // open: eq, lt
  and and_2 (and_2_out, comparator_3_lt, comparator_2_gt);
  Comparator #(.mode("unsigned"), .width(4)) comparator_2 (
    .a(out_37), .b(4'b0000), .gt(comparator_2_gt));  // open: eq, lt
  D_Flip_Flop d_ff_1 (.D(comparator_1_gt), .clk(and_3_out), .Qn(out_22), .reset(Reset));  // open: Q, preset
  and and_3 (and_3_out, Main_Clock, out_32[2]);
  Multiplexer #(.enable("false"), .select(2)) multiplexer_1 (
    .in0(1'b0), .in1(adder_1_cout), .in2(1'b0), .in3(comparator_4_gt), .out(multiplexer_1_out[0]),
    .sel(out_37[1:0]));
  Comparator #(.mode("unsigned"), .width(4)) comparator_3 (
    .a(out_37), .b(4'b0100), .lt(comparator_3_lt));  // open: gt, eq
  Adder #(.width(16)) adder_1 (.a(out_23), .b(out_24), .out(out_28), .cout(adder_1_cout));  // open: cin
  Counter #(.max('hffff), .width(16)) counter_2 (
    .clr(Reset), .load(multiplexer_2_out), .up(1'b1), .count(out_32[1]), .clk(Main_Clock),
    .D(controlled_buffer_1_out), .Q(counter_2_q));  // open: carry
  DotMatrix #(.dotshape("circle"), .inputtype("row"), .matrixcols(16), .matrixrows(1)) dotmatrix_4 (.row0(out_23));
  Subtractor #(.width(16)) subtractor_1 (
    .a(out_23), .b(out_24), .out(out_29), .bout(multiplexer_1_out[1]));  // open: bin
  not not_1 (not_1_out, out_3[1]);
  not not_2 (not_2_out, out_3[0]);
  not not_3 (not_3_out, out_22);
  Multiplexer #(.enable("false"), .select(4)) multiplexer_2 (
    .in0(1'b0), .in1(1'b1), .in2(out_22), .in3(not_3_out), .in4(out_3[1]), .in5(not_1_out), .in6(out_3[0]),
    .in7(not_2_out), .in8(1'b0), .in9(1'b0), .in10(1'b0), .in11(1'b0), .in12(1'b0), .in13(1'b0), .in14(1'b0),
    .in15(1'b0), .out(multiplexer_2_out), .sel(out_5));
  Register #(.width(16)) register_2 (
    .D(controlled_buffer_1_out), .en(out_32[2]), .clk(Main_Clock), .Q(out_23), .clr(Reset));
  Comparator #(.mode("unsigned"), .width(16)) comparator_4 (
    .a(multiplier_1_cout), .b({16{1'b0}}), .gt(comparator_4_gt));  // open: eq, lt
  assign controlled_buffer_1_out = out_32[3] ? out_23 : 16'bz;  // Controlled_Buffer controlled_buffer_4
  Multiplier #(.width(16)) multiplier_1 (.a(out_23), .b(out_24), .out(out_25), .cout(multiplier_1_cout));  // open: cin
  assign controlled_buffer_1_out = out_32[0] ? counter_2_q : 16'bz;  // Controlled_Buffer controlled_buffer_5
  Divider #(.width(16)) divider_1 (.a(out_23), .b(out_24), .out(_0100), .rem(_0101));  // open: upper
  Register #(.width(16)) register_3 (
    .D(controlled_buffer_1_out), .en(out_32[4]), .clk(Main_Clock), .Q(out_24), .clr(Reset));
  Multiplexer #(.enable("false"), .select(4), .width(16)) multiplexer_3 (
    .in1(out_28), .in2(out_29), .in3(out_25), .in4(_0100), .in5(_0101), .out(controlled_buffer_1_out),
    .sel(out_37));  // open: in0, in6, in7, in8, in9, in10, in11, in12, in13, in14, in15
  assign controlled_buffer_1_out = out_32[5] ? out_24 : 16'bz;  // Controlled_Buffer controlled_buffer_6
  Clock clock_1 (.out(clock_1_out));
  D_Flip_Flop d_ff_2 (.D(out_32[13]), .clk(Main_Clock), .Qn(d_ff_2_qn), .reset(Reset));  // open: Q, preset
  and and_4 (Main_Clock, clock_1_out, d_ff_2_qn);
  Counter #(.max('hffffffff), .width(32)) counter_3 (
    .load(1'b0), .count(1'b1), .Q(Cycle_count), .up(1'b1), .clk(Main_Clock), .clr(Reset));  // open: D, carry

  assign out_33 = out_32[0];
  assign out_34 = out_32[1];
  assign out_35 = out_32[2];
  assign out_36 = out_32[3];
  assign out_38 = out_32[4];
  assign out_39 = out_32[5];
  assign out_40 = out_32[6];
  assign out_41 = out_32[7];
  assign out_42 = out_32[8];
  assign out_43 = out_32[9];
  assign out_44 = out_32[10];
  assign out_45 = out_32[11];
  assign out_46 = out_32[12];
  assign out_47 = out_32[13];
  assign out_48 = out_32[14];
  assign out_49 = out_37;
  assign out_50 = out_5;

  // Other names for the same wires on the sheet: A_ZFlag = out_22; ALU_CW[3:0] = out_37; ALU_Flags[1:0] = out_3;
  //   JMP_CW[3:0] = out_5; Counter_Out = out_32[0]; Counter_Enable = out_32[1]; A_In = out_32[2]; A_Out = out_32[3];
  //   B_In = out_32[4]; B_Out = out_32[5]; Mem_In = out_32[6]; Mem_Out = out_32[7]; MAR_In = out_32[8];
  //   IR_In = out_32[9]; IDR_In = out_32[10]; IDR_Out = out_32[11]; Instr_Reset = out_32[12]; Halt = out_32[13];
  //   Out_In = out_32[14]

  // Notes on the sheet:
  //   contents of Microcode (hex, n*v repeats v):
  //   101 282 1000 15*0 101 482 1804 13*0 101 482 900 1084 12*0 101 482 900 1048 12*0 5008 15*0 101 482
  //   900 5040 12*0 2000 159*0 101 482 900 90 101004 11*0 101 482 810 101004 12*0 101 482 900 90 201004
  //   11*0 101 482 810 201004 12*0 101 482 900 90 301004 11*0 101 482 810 301004 12*0 101 482 900 90
  //   401004 11*0 101 482 810 401004 12*0 101 482 900 90 501004 11*0 101 482 810 501004 108*0 101 482
  //   181800 13*0 101 482 281800 13*0 101 482 381800 13*0 101 482 481800 13*0 101 482 581800 13*0 101 482
  //   681800 13*0 101 482 781800
  //   Instruction
  //   Timestep
  //   Controlword
  //   Register A
  //   Register B
  //   0001
  //   0010
  //   0011
endmodule
