// Logisim project CPU2_v2.circ as structural Verilog: 1 circuit, main circuit main
module main (
  input  Bus_Override,
  input  [15:0] in_2,
  output [1:0] ALU_Flags,
  output [3:0] out_4,
  output [31:0] Cycle_Count,
  output [15:0] Bus_Contents,
  output [15:0] out_7,
  output [15:0] out_8,
  output [15:0] out_9,
  output [15:0] out_10,
  output [15:0] out_11,
  output [15:0] out_12,
  output [15:0] out_13,
  output [15:0] out_14,
  output [15:0] out_15,
  output [15:0] out_16,
  output [15:0] out_17,
  output [15:0] out_18,
  output [15:0] out_19,
  output [15:0] out_20,
  output [15:0] out_21,
  output [15:0] out_22,
  output [15:0] out_23,
  output [15:0] out_24,
  output [31:0] Instruction,
  output [3:0] out_26,
  output [23:0] Control_Word,
  output Counter_Out,
  output Counter_Enable,
  output A_In,
  output A_Out,
  output B_In,
  output B_Out,
  output [3:0] out_34,
  output Mem_In,
  output Mem_Out,
  output MAR_In,
  output IR_In,
  output IDR_In,
  output IDR_Out,
  output Instr_Reset,
  output Halt,
  output Out_In,
  output [3:0] ALU_CW_Probe,
  output [3:0] JMP_CW_Probe
);

  wire A_ZFlag, adder_1_cout, and_2_out, and_3_out, clock_1_out, comparator_1_gt, comparator_2_gt,
       comparator_3_lt, comparator_4_gt, d_ff_1_qn, Main_Clock, multiplexer_4_out, not_1_out, not_2_out,
       not_3_out, or_1_out, or_2_out, Reset;
  wire [1:0] multiplexer_3_out;
  wire [15:0] adder_1_out, divider_1_out, divider_1_rem, Memory_Addr_Reg_q, multiplexer_1_out,
       multiplexer_2_out, multiplier_1_cout, multiplier_1_out, Program_Counter_q, ram_1_dout,
       subtractor_1_out;

  Counter #(.max('hf), .width(4)) Instruction_Timestep (
    .clr(Reset), .load(Control_Word[12]), .up(1'b1), .count(1'b1), .clk(Main_Clock), .D(4'b0000), .Q(out_26));  // open: carry
  RAM #(.addrWidth(16), .dataWidth(16), .enables("line")) ram_1 (
    .addr(Memory_Addr_Reg_q), .we(Control_Word[6]), .clk(Main_Clock), .din(Bus_Contents), .dout(ram_1_dout));
  Clock clock_1 (.out(clock_1_out));
  D_Flip_Flop d_ff_1 (.D(Control_Word[13]), .clk(Main_Clock), .Qn(d_ff_1_qn), .reset(Reset));  // open: Q, preset
  Multiplexer #(.enable("false"), .width(16)) multiplexer_1 (
    .in0(Bus_Contents), .in1({16{1'b0}}), .out(multiplexer_1_out), .sel(Control_Word[12]));
  or or_1 (or_1_out, Control_Word[9], Control_Word[12]);
  and and_1 (Main_Clock, clock_1_out, d_ff_1_qn);
  Register #(.width(16)) Instr_Reg (
    .D(multiplexer_1_out), .en(or_1_out), .clk(Main_Clock), .Q(Instruction[31:16]), .clr(Reset));
  ROM #(.addrWidth(20), .dataWidth(24)) Microcode (
    .addr({Instruction[31:16], out_26}),
    .data({Control_Word[23:6], B_Out, B_In, A_Out, A_In, Control_Word[1:0]}));
  Button button_1 (.out(Reset));
  Counter #(.max('hffffffff), .width(32)) counter_1 (
    .load(1'b0), .count(1'b1), .Q(Cycle_Count), .up(1'b1), .clk(Main_Clock), .clr(Reset));  // open: D, carry
  assign Bus_Contents = Control_Word[7] ? ram_1_dout : 16'bz;  // Controlled_Buffer controlled_buffer_1
  Register #(.width(16)) InstrData_Reg (
    .D(multiplexer_2_out), .en(or_2_out), .clk(Main_Clock), .Q(Instruction[15:0]), .clr(Reset));
  Multiplexer #(.enable("false"), .width(16)) multiplexer_2 (
    .in0(Bus_Contents), .in1({16{1'b0}}), .out(multiplexer_2_out), .sel(Control_Word[12]));
  or or_2 (or_2_out, Control_Word[10], Control_Word[12]);
  Register #(.width(16)) Memory_Addr_Reg (
    .D(Bus_Contents), .en(Control_Word[8]), .clk(Main_Clock), .Q(Memory_Addr_Reg_q), .clr(Reset));
  assign Bus_Contents = Control_Word[11] ? Instruction[15:0] : 16'bz;  // Controlled_Buffer controlled_buffer_2
  DotMatrix #(.dotshape("circle"), .inputtype("row"), .matrixcols(16), .matrixrows(2)) dotmatrix_1 (
    .row0(Instruction[31:16]), .row1(Instruction[15:0]));
  DotMatrix #(.inputtype("row"), .matrixcols(24), .matrixrows(1)) dotmatrix_2 (.row0({Control_Word[23:6], B_Out, B_In, A_Out, A_In, Control_Word[1:0]}));
  Demultiplexer #(.enable("false"), .width(4)) demultiplexer_1 (
    .out0(ALU_CW_Probe), .out1(JMP_CW_Probe), .in(Control_Word[23:20]), .sel(Control_Word[19]));
  // Shift_Register #(.length(16), .width(16)) shift_register_1: pin names not known; wires that end beside it: Reset, 1'b0, Control_Word[14], Main_Clock, Bus_Contents, out_7, out_8, out_9, out_10, out_11, out_12, out_13, out_14, out_15, out_16, out_17, out_18
  Pull_Resistor pull_resistor_1 (.node(Bus_Contents));
  assign Bus_Contents = Bus_Override ? in_2 : 16'bz;  // Controlled_Buffer controlled_buffer_3
  Register #(.width(2)) register_1 (
    .D(multiplexer_3_out), .en(and_2_out), .clk(Main_Clock), .Q(ALU_Flags), .clr(Reset));
  Comparator #(.mode("unsigned"), .width(16)) comparator_1 (
    .a(Bus_Contents), .b({16{1'b0}}), .gt(comparator_1_gt));  // open: eq, lt
  and and_2 (and_2_out, comparator_3_lt, comparator_2_gt);
  Comparator #(.mode("unsigned"), .width(4)) comparator_2 (
    .a(ALU_CW_Probe), .b(4'b0000), .gt(comparator_2_gt));  // open: eq, lt
  D_Flip_Flop u_A_ZFlag (.D(comparator_1_gt), .clk(and_3_out), .Qn(A_ZFlag), .reset(Reset));  // open: Q, preset
  and and_3 (and_3_out, Main_Clock, A_In);
  Multiplexer #(.enable("false"), .select(2)) multiplexer_3 (
    .in0(1'b0), .in1(adder_1_cout), .in2(1'b0), .in3(comparator_4_gt), .out(multiplexer_3_out[0]),
    .sel(ALU_CW_Probe[1:0]));
  Comparator #(.mode("unsigned"), .width(4)) comparator_3 (
    .a(ALU_CW_Probe), .b(4'b0100), .lt(comparator_3_lt));  // open: gt, eq
  Adder #(.width(16)) adder_1 (.a(out_23), .b(out_24), .out(adder_1_out), .cout(adder_1_cout));  // open: cin
  Counter #(.max('hffff), .width(16)) Program_Counter (
    .clr(Reset), .load(multiplexer_4_out), .up(1'b1), .count(Control_Word[1]), .clk(Main_Clock),
    .D(Bus_Contents), .Q(Program_Counter_q));  // open: carry
  Subtractor #(.width(16)) subtractor_1 (
    .a(out_23), .b(out_24), .out(subtractor_1_out), .bout(multiplexer_3_out[1]));  // open: bin
  not not_1 (not_1_out, ALU_Flags[1]);
  not not_2 (not_2_out, ALU_Flags[0]);
  not not_3 (not_3_out, A_ZFlag);
  Multiplexer #(.enable("false"), .select(4)) multiplexer_4 (
    .in0(1'b0), .in1(1'b1), .in2(A_ZFlag), .in3(not_3_out), .in4(ALU_Flags[1]), .in5(not_1_out),
    .in6(ALU_Flags[0]), .in7(not_2_out), .in8(1'b0), .in9(1'b0), .in10(1'b0), .in11(1'b0), .in12(1'b0),
    .in13(1'b0), .in14(1'b0), .in15(1'b0), .out(multiplexer_4_out), .sel(JMP_CW_Probe));
  Register #(.width(16)) A_Register (.D(Bus_Contents), .en(A_In), .clk(Main_Clock), .Q(out_23), .clr(Reset));
  Comparator #(.mode("unsigned"), .width(16)) comparator_4 (
    .a(multiplier_1_cout), .b({16{1'b0}}), .gt(comparator_4_gt));  // open: eq, lt
  assign Bus_Contents = A_Out ? out_23 : 16'bz;  // Controlled_Buffer controlled_buffer_4
  Multiplier #(.width(16)) multiplier_1 (
    .a(out_23), .b(out_24), .out(multiplier_1_out), .cout(multiplier_1_cout));  // open: cin
  assign Bus_Contents = Control_Word[0] ? Program_Counter_q : 16'bz;  // Controlled_Buffer controlled_buffer_5
  Divider #(.width(16)) divider_1 (.a(out_23), .b(out_24), .out(divider_1_out), .rem(divider_1_rem));  // open: upper
  Register #(.width(16)) B_Register (.D(Bus_Contents), .en(B_In), .clk(Main_Clock), .Q(out_24), .clr(Reset));
  Multiplexer #(.enable("false"), .select(4), .width(16)) multiplexer_5 (
    .in1(adder_1_out), .in2(subtractor_1_out), .in3(multiplier_1_out), .in4(divider_1_out),
    .in5(divider_1_rem), .out(Bus_Contents), .sel(ALU_CW_Probe));  // open: in0, in6, in7, in8, in9, in10, in11, in12, in13, in14, in15
  assign Bus_Contents = B_Out ? out_24 : 16'bz;  // Controlled_Buffer controlled_buffer_6

  assign Control_Word[5:2] = {B_Out, B_In, A_Out, A_In};
  assign Counter_Enable = Control_Word[1];
  assign Counter_Out = Control_Word[0];
  assign Halt = Control_Word[13];
  assign IDR_In = Control_Word[10];
  assign IDR_Out = Control_Word[11];
  assign Instr_Reset = Control_Word[12];
  assign IR_In = Control_Word[9];
  assign MAR_In = Control_Word[8];
  assign Mem_In = Control_Word[6];
  assign Mem_Out = Control_Word[7];
  assign out_4 = JMP_CW_Probe;
  assign out_34 = ALU_CW_Probe;
  assign Out_In = Control_Word[14];

  // Other names for the same wires on the sheet: ALU_CW[3:0] = ALU_CW_Probe; Counter_Out_t = Control_Word[0];
  //   Counter_Enable_t = Control_Word[1]; A_In_t = A_In; A_Out_t = A_Out; B_In_t = B_In; B_Out_t = B_Out;
  //   Mem_In_t = Control_Word[6]; Mem_Out_t = Control_Word[7]; MAR_In_t = Control_Word[8]; IR_In_t = Control_Word[9];
  //   IDR_In_t = Control_Word[10]; IDR_Out_t = Control_Word[11]; Instr_Reset_t = Control_Word[12];
  //   Halt_t = Control_Word[13]; Out_In_t = Control_Word[14]; JMP_CW[3:0] = JMP_CW_Probe

  // Notes on the sheet:
  //   contents of Microcode (hex, n*v repeats v):
  //   101 282 16*1000 101 482 1804 13*0 101 482 900 1084 12*0 101 482 900 1048 12*0 5008 15*0 101 482 900
  //   5040 12*0 2000 159*0 101 482 900 90 101004 11*0 101 482 810 101004 12*0 101 482 900 90 201004 11*0
  //   101 482 810 201004 12*0 101 482 900 90 301004 11*0 101 482 810 301004 12*0 101 482 900 90 401004
  //   11*0 101 482 810 401004 12*0 101 482 900 90 501004 11*0 101 482 810 501004 108*0 101 482 181800 13*0
  //   101 482 281800 13*0 101 482 381800 13*0 101 482 481800 13*0 101 482 581800 13*0 101 482 681800 13*0
  //   101 482 781800
  //   Timestep
  //   Register A
  //   Register B
  //   0001
  //   0010
  //   0011
  //   0100
  //   0101
endmodule
